# Fritzing sketch Nucleo-F446_I2C_AQM1602 (saved by Fritzing 0.9.3b)
breadboards: 1

parts:
  LCD1 = LCD screen  # not connected
  J1 = female pin header, 4 pins [form="♀ (female)"]
  J2 = STM32 Nucleo boards
  R1 = Resistor [tolerance=±5% resistance=4.7k package=THT]
  R2 = Resistor [tolerance=±5% resistance=4.7k package=THT]

nets:
  N1: J1.pin1, J2.GND
  N2: J1.pin2, J2.A4/SDA, R1.Pin_0
  N3: J1.pin3, J2.A5/SCL, R2.Pin_0
  N4: J1.pin4, J2.3V3, R1.Pin_1, R2.Pin_1

notes:
  AQM1602
  1 +V
  2 SCL
  3 SDA
  4 GND
