# Fritzing sketch STM32Cube_u8g2_SSD1306 (saved by Fritzing 0.9.3b)
breadboards: 1

parts:
  J1 = STM32 Nucleo boards
  U1 = LCD-16X2 [package=lcd-8x2]  # not connected
  J2 = female pin header, 7 pins [form="♀ (female)"]
  C1 = Electrolytic Capacitor [capacitance=1µF package="100 mil [THT, electrolytic]"]

nets:
  N1: J1.D8, J2.pin5
  N2: J1.D9_PWM, J2.pin6
  N3: J1.D10_PWM/SS, J2.pin7
  N4: J1.D11_PWM/MOSI, J2.pin4
  N5: J1.D13/SCK, J2.pin3
  N6: J1.3V3, J2.pin2, C1.+
  N7: J1.GND, J2.pin1, C1.-

notes:
  SSD1306 OLED
  1 GND
  2 VCC
  3 D0 (SCK)
  4 D1 (MOSI)
  5 RES
  6 DC
  7 CS
