# Fritzing sketch STM32_MCP3208 (saved by Fritzing 0.9.3b)
breadboards: 1
perfboards: 1

parts:
  IC1 = IC, DIP package, 16 pins [chip_label=MCP3208]
  C1 = Ceramic Capacitor [capacitance=100nF package="100 mil [THT, multilayer]"]
  R1 = Rotary Potentiometer (Small) [maximum_resistance=100kΩ package=THT]  # not connected
  R2 = Rotary Potentiometer (Small) [maximum_resistance=100kΩ package=THT]  # not connected
  R3 = Rotary Potentiometer (Small) [maximum_resistance=100kΩ package=THT]  # not connected
  J1 = STM32 Nucleo boards
  C2 = Electrolytic Capacitor [capacitance=1µF package="100 mil [THT, electrolytic]"]
  R4 = Resistor [tolerance=±5% resistance=2.2k package=THT]

nets:
  N1: IC1.pin10, J1.D10_PWM/SS
  N2: IC1.pin11, J1.D11_PWM/MOSI
  N3: IC1.pin12, J1.D12/MISO, R4.Pin_1
  N4: IC1.pin13, J1.D13/SCK
  N5: IC1.pin14, C1.0, J1.GND, C2.-, R4.Pin_0
  N6: IC1.pin15, IC1.pin16, C1.1, J1.3V3, C2.+

notes:
  MCP3208
  1 CH0 16 VDD
  2 CH1 15 VREF
  3 CH2 14 AGND
  4 CH3 13 CLK
  5 CH4 12 DOUT
  6 CH5 11 DIN
  7 CH6 10 !CS/SHDN
  8 CH7 9 DGND
  POTx3
