# Fritzing sketch STM32_MCP4922 (saved by Fritzing 0.9.3b)
breadboards: 1

parts:
  J1 = STM32 Nucleo boards
  IC1 = IC, DIP package, 14 pins [chip_label=MCP4922]
  C1 = Electrolytic Capacitor [capacitance=1µF package="100 mil [THT, electrolytic]"]
  C2 = Ceramic Capacitor [capacitance=100nF package="100 mil [THT, multilayer]"]

nets:
  N1: J1.D9_PWM, IC1.pin8
  N2: J1.D10_PWM/SS, IC1.pin3
  N3: J1.D11_PWM/MOSI, IC1.pin5
  N4: J1.D13/SCK, IC1.pin4
  N5: J1.5V, IC1.pin1, IC1.pin9, IC1.pin11, IC1.pin13, C1.+, C2.1
  N6: J1.GND, IC1.pin12, C1.-, C2.0

notes:
  MCP4922
  1 VDD 14 VOUTA
  2 NC 13 VREFA
  3 !CS 12 AVSS
  4 SCK 11 VREFB
  5 SDI 10 VOUTB
  6 NC 9 !SHDN
  7 NC 8 !LDAC
  OUT1
  OUT2
